# Fritzing sketch RGBakonexioak (saved by Fritzing 0.8.7b)
breadboards: 1

parts:
  LED1 = RGB LED (com. cathode, rgb) [package="5 mm [THT]"]
  R1 = Resistor [tolerance=±5% resistance=220 package=THT]
  R2 = Resistor [tolerance=±5% resistance=220 package=THT]
  R3 = Resistor [tolerance=±5% resistance=220 package=THT]
  Parte1 = Icezum Alhambra

nets:
  N1: LED1.red_anode, LED1.green_anode, LED1.blue_anode, R1.Pin_0, R2.Pin_0, R3.Pin_0
  N2: LED1.common_cathode, Parte1.5V
  N3: R1.Pin_1, R2.Pin_1, R3.Pin_1, Parte1.D0, Parte1.D1, Parte1.D2

notes:
  RGBaren 1.(gorria), 3.(berdea) eta 4. (urdina) borneei 220 Ohmeko erresistentzia konektatzen zaie seriean.
  RGBaren 2. bornea plakaren 5Vra konektatuko da

custom parts:
  Icezum Alhambra: The Arduino Uno is a microcontroller board based on the ATmega328 (datasheet). It has 14 digital input/output pins (of which 6 can be used as PWM outputs), 6 analog inputs, a 16 MHz ceramic resonator, a USB connection, a power jack, an ICSP header, and a reset button. It contains everything needed to support the microcontroller; simply connect it to a computer with a USB cable or power it with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
