# Fritzing sketch 7_segmentuko_display_anodoa (saved by Fritzing 0.8.7b)
breadboards: 1

parts:
  7_Segment5 = 7 Segment Display
  R1 = Resistor [tolerance=±5% resistance=220 package=THT]
  Parte1 = iceZUM Alhambra

nets:
  N1: 7_Segment5.Segment_E, Parte1.D5
  N2: 7_Segment5.Segment_D, Parte1.D6
  N3: 7_Segment5.common_cathode, R1.Pin_1
  N4: 7_Segment5.Segment_C, Parte1.D7, Parte1.V7
  N5: 7_Segment5.Segment_B, Parte1.D8, Parte1.V8
  N6: 7_Segment5.Segment_A, Parte1.D9
  N7: 7_Segment5.Segment_F, Parte1.D4
  N8: 7_Segment5.Segment_G, Parte1.D3
  N9: R1.Pin_0, Parte1.3V3

notes:
  Erresistentzia 330 edo 220 Ohm.

custom parts:
  iceZUM Alhambra: Arduino/zum compatible Open FPGA electronic board. Synthesize hardware easily, using only open source tools
