# Fritzing sketch Display4digAlhambra (saved by Fritzing 0.8.7b)
breadboards: 1

parts:
  U1 = 7-SEGMENT-4DIGIT [package=7-segment-4digit-youngsun]
  R3 = Resistor [tolerance=±5% resistance=220 package=THT]
  R4 = Resistor [tolerance=±5% resistance=220 package=THT]
  R5 = Resistor [tolerance=±5% resistance=220 package=THT]
  R6 = Resistor [tolerance=±5% resistance=220 package=THT]
  Parte1 = Icezum Alhambra

nets:
  N1: U1.3, Parte1.D4
  N2: U1.4, Parte1.D3
  N3: U1.6, Parte1.D2
  N4: U1.7, Parte1.D6
  N5: U1.8, R6.Pin_0
  N6: U1.9, Parte1.D1
  N7: U1.11, R4.Pin_1
  N8: U1.13, Parte1.D0
  N9: U1.14, R5.Pin_1
  N10: R3.Pin_0, Parte1.D11
  N11: R4.Pin_0, Parte1.D12
  N12: R5.Pin_0, Parte1.D13
  N13: R6.Pin_1, Parte1.D10

notes:
  Erresistentziak 1000 Ohm-ekoak dira.

custom parts:
  Icezum Alhambra: The Arduino Uno is a microcontroller board based on the ATmega328 (datasheet). It has 14 digital input/output pins (of which 6 can be used as PWM outputs), 6 analog inputs, a 16 MHz ceramic resonator, a USB connection, a power jack, an ICSP header, and a reset button. It contains everything needed to support the microcontroller; simply connect it to a computer with a USB cable or power it with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
